// Logisim project T1 Tomas_Maturana.circ as structural Verilog: 1 circuit, main circuit main
module main (
  input  X3,
  input  X2,
  input  X1,
  input  X0,
  output Z
);

  wire and_1_out, and_2_out, and_3_out, and_4_out, and_5_out, and_6_out, not_1_out, not_2_out, not_3_out,
       not_4_out;

  not not_1 (not_1_out, X1);
  not not_2 (not_2_out, X0);
  not not_3 (not_3_out, X3);
  not not_4 (not_4_out, X2);
  and and_1 (and_1_out, not_2_out, not_4_out, X3);
  and and_2 (and_2_out, not_1_out, not_4_out, X3);
  and and_3 (and_3_out, not_2_out, not_1_out, X3);
  and and_4 (and_4_out, not_2_out, X1, not_3_out);
  and and_5 (and_5_out, not_1_out, X2, not_3_out);
  and and_6 (and_6_out, not_4_out, not_3_out);
  or or_1 (Z, and_1_out, and_2_out, and_3_out, and_4_out, and_5_out, and_6_out);
endmodule
