// Logisim project T2 Tomas_Maturana.circ as structural Verilog: 5 circuits, main circuit DIVFREC
module DIVFREC (
  input  X1,
  input  X0,
  output clkout
);

  wire circuito_combinacional_1_d0, circuito_combinacional_1_d1, clock_1_out, D0_Q0_q, D1_Q1_q;

  circuito_combinacional circuito_combinacional_1 (
    .X1(X1), .X0(X0), .Q0(D0_Q0_q), .Q1(D1_Q1_q), .clkout(clkout), .D0(circuito_combinacional_1_d0),
    .D1(circuito_combinacional_1_d1));
  Register #(.width(1)) D0_Q0 (.D(circuito_combinacional_1_d0), .Q(D0_Q0_q), .clk(clock_1_out));  // open: en, clr
  Register #(.width(1)) D1_Q1 (.D(circuito_combinacional_1_d1), .Q(D1_Q1_q), .clk(clock_1_out));  // open: en, clr
  Clock clock_1 (.out(clock_1_out));
endmodule

module circuito_combinacional (
  input  X1,
  input  X0,
  input  Q0,
  input  Q1,
  output clkout,
  output D0,
  output D1
);

  clkout clkout_1 (.X1(X1), .X0(X0), .Q0(Q0), .Q1(Q1), .clkout(clkout));
  D0 d0_1 (.X1(X1), .X0(X0), .Q0(Q0), .Q1(Q1), .D0(D0));
  D1 d1_1 (.X1(X1), .X0(X0), .Q0(Q0), .Q1(Q1), .D1(D1));
endmodule

module clkout (
  input  X1,
  input  X0,
  input  Q0,
  input  Q1,
  output clkout
);

  wire and_1_out, and_2_out, and_3_out, not_1_out, not_2_out, not_3_out, not_4_out;

  not not_1 (not_1_out, Q1);
  not not_2 (not_2_out, Q0);
  not not_3 (not_3_out, X1);
  not not_4 (not_4_out, X0);
  and and_1 (and_1_out, Q0, X1, not_4_out);
  and and_2 (and_2_out, X0, Q0, not_1_out);
  and and_3 (and_3_out, not_2_out, Q1, not_3_out, not_4_out);
  or or_1 (clkout, and_1_out, and_2_out, and_3_out);
endmodule

module D0 (
  input  X1,
  input  X0,
  input  Q0,
  input  Q1,
  output D0
);

  wire and_1_out, and_2_out, and_3_out, not_1_out, not_2_out;

  not not_1 (not_1_out, Q1);
  not not_2 (not_2_out, Q0);
  and and_1 (and_1_out, not_2_out, Q1, X0);
  and and_2 (and_2_out, not_2_out, Q1, X1);
  and and_3 (and_3_out, Q0, not_1_out, X1);
  or or_1 (D0, and_1_out, and_2_out, and_3_out);
endmodule

module D1 (
  input  X1,
  input  X0,
  input  Q0,
  input  Q1,
  output D1
);

  wire and_1_out, and_2_out, and_3_out, not_1_out, not_2_out, not_3_out, not_4_out;

  not not_1 (not_1_out, Q1);
  not not_2 (not_2_out, Q0);
  not not_3 (not_3_out, X1);
  not not_4 (not_4_out, X0);
  and and_1 (and_1_out, not_2_out, not_1_out);
  and and_2 (and_2_out, Q0, Q1, not_3_out);
  and and_3 (and_3_out, Q0, not_1_out, not_4_out);
  or or_1 (D1, and_1_out, and_2_out, and_3_out);
endmodule
