// Logisim project T3_Tomas_Maturana.circ as structural Verilog: 1 circuit, main circuit main
module main (
  input  [7:0] D0__D7,
  input  START,
  output ERR,
  output RDY,
  output [2:0] Z0___Z2
);

  wire clock_1_out, comparator_1_eq;
  wire [2:0] adder_1_out, multiplexer_2_out, multiplexer_3_out;
  wire [7:0] multiplexer_1_out, RD_q, shifter_1_out, shifter_2_out;

  Shifter #(.shift("lr")) shifter_1 (.in(RD_q), .\dist (3'b001), .out(shifter_1_out));
  Multiplexer #(.width(8), .enable("false")) multiplexer_1 (
    .in0(shifter_1_out), .in1(shifter_2_out), .out(multiplexer_1_out), .sel(START));
  Shifter #(.shift("lr")) shifter_2 (.in(D0__D7), .\dist (3'b001), .out(shifter_2_out));
  Multiplexer #(.width(3), .enable("false")) multiplexer_2 (
    .in0(adder_1_out), .in1(3'b000), .out(multiplexer_2_out), .sel(START));
  Register RD (.D(multiplexer_1_out), .Q(RD_q), .clk(clock_1_out));  // open: en, clr
  Clock clock_1 (.out(clock_1_out));
  Register #(.width(3)) RZ (.D(multiplexer_2_out), .Q(Z0___Z2), .clk(clock_1_out));  // open: en, clr
  Comparator comparator_1 (.a(RD_q), .b({8{1'b0}}), .eq(comparator_1_eq));  // open: gt, lt
  Multiplexer #(.width(3), .enable("false")) multiplexer_3 (
    .in0(3'b001), .in1(3'b000), .out(multiplexer_3_out), .sel(comparator_1_eq));
  Adder #(.width(3)) adder_1 (.a(Z0___Z2), .b(multiplexer_3_out), .out(adder_1_out));  // open: cin, cout
  Comparator comparator_2 (.a(D0__D7), .b({8{1'b0}}), .eq(ERR));  // open: gt, lt
  or or_1 (RDY, ERR, comparator_1_eq);
endmodule
