// Logisim project c1 p2.circ as structural Verilog: 1 circuit, main circuit main
module main (
  input  in_1,
  output [7:0] out_2
);

  wire and_1_out, clock_1_out, comparator_1_eq, not_1_out;

  Clock clock_1 (.out(clock_1_out));
  Comparator #(.width(1)) comparator_1 (.a(in_1), .b(1'b1), .eq(comparator_1_eq));  // open: gt, lt
  Counter counter_1 (.D(out_2), .Q(out_2), .clk(clock_1_out), .clr(and_1_out));  // open: load, count, carry
  and and_1 (and_1_out, not_1_out, comparator_1_eq);
  not not_1 (not_1_out, clock_1_out);
endmodule
